// Logisim project cpu.circ as structural Verilog: 15 circuits, main circuit main
module main (
  input  Rst
);

  wire and_1_out, Clk_out, HLT, not_1_out;
  wire [7:0] alu_1_ao, alu_1_ro, ar_1_adho, ar_1_adlo, dp_1_adho, dp_1_adlo, memory_1_do;

  Clock Clk (.out(Clk_out));
  LED u_Hlt (.in(HLT));
  not not_1 (not_1_out, HLT);
  and and_1 (and_1_out, Clk_out, not_1_out);
  IR ir_1 (.DI(memory_1_do), .Clk(and_1_out), .Reset(Rst));  // open: DO, WE
  Memory memory_1 (
    .DO(memory_1_do), .Clk(and_1_out), .DI(memory_1_do), .ADL(dp_1_adlo), .ADH(dp_1_adho));  // open: WE, OE
  ALU alu_1 (.RO(alu_1_ro), .AO(alu_1_ao), .DBI(memory_1_do), .AI(alu_1_ao));  // open: C, Z, OpS
  R r_1 (.out_8(memory_1_do), .DBI(memory_1_do), .RI(alu_1_ro), .Clk(and_1_out), .Rst(Rst));  // open: RWE, DWE, OE
  A a_1 (
    .DBO(memory_1_do), .RO(alu_1_ao), .DBI(memory_1_do), .RI(alu_1_ao), .Clk(and_1_out), .Rst(Rst));  // open: RWE, DWE, ROE, DOE
  DP dp_1 (
    .ADLO(dp_1_adlo), .ADHO(dp_1_adho), .ADLI(ar_1_adlo), .ADHI(ar_1_adho), .Clk(and_1_out), .Rst(Rst));  // open: WE
  XY xy_1 (.DBO(memory_1_do), .DBI(memory_1_do), .Clk(and_1_out), .Reset(Rst));  // open: XWE, YWE, XOE, YOE
  AR ar_1 (.ADLO(ar_1_adlo), .ADHO(ar_1_adho), .ADLI(memory_1_do), .Clk(and_1_out), .Rst(Rst));  // open: LWE, HWE, OE
  PC pc_1 (
    .ADLO(ar_1_adlo), .ADHO(ar_1_adho), .ADO(memory_1_do), .Reset(Rst), .Clk(and_1_out), .ADLI(ar_1_adlo),
    .ADHI(ar_1_adho));  // open: ABWE, CE, AOE, LOE, HOE
  Latch latch_1 (
    .DBO(memory_1_do), .ADLO(ar_1_adlo), .ADHO(ar_1_adho), .DBI(memory_1_do), .ADLI(ar_1_adlo),
    .ADHI(ar_1_adho));  // open: CL, CH
  SP sp_1 (
    .AHO(ar_1_adho), .ALO(ar_1_adlo), .DO(memory_1_do), .DI(memory_1_do), .Clk(and_1_out), .Rst(Rst));  // open: WE, IE, DE, AOE, DOE
  SR sr_1 (.DO(memory_1_do), .HO(HLT), .DI(memory_1_do), .Clk(and_1_out), .Rst(Rst));  // open: FO, IO, WE, FS
endmodule

module PC (
  input  Reset,
  input  ABWE,
  input  CE,
  input  Clk,
  input  AOE,
  input  [7:0] ADLI,
  input  [7:0] ADHI,
  input  LOE,
  input  HOE,
  output [7:0] ADLO,
  output [7:0] ADHO,
  output [7:0] ADO
);

  wire [7:0] multiplexer_1_out;
  wire [15:0] counter_1_q;

  Counter #(.max('hffff), .width(16)) counter_1 (
    .clr(Reset), .load(ABWE), .up(1'b1), .count(CE), .clk(Clk), .D({ADHI, ADLI}), .Q(counter_1_q));  // open: carry
  assign {ADHO, ADLO} = AOE ? counter_1_q : 16'bz;  // Controlled_Buffer controlled_buffer_1
  Multiplexer #(.width(8)) multiplexer_1 (
    .in0(counter_1_q[7:0]), .in1(counter_1_q[15:8]), .out(multiplexer_1_out), .sel(HOE));
  assign ADO = LOE ? multiplexer_1_out : 8'bz;  // Controlled_Buffer controlled_buffer_2
endmodule

module Memory (
  input  WE,
  input  Clk,
  input  [7:0] DI,
  input  OE,
  input  [7:0] ADL,
  input  [7:0] ADH,
  output [7:0] DO
);

  wire and_1_out, not_1_out, not_2_out;
  wire [7:0] controlled_buffer_1_out, ram_1_dout, rom_1_data;

  not not_1 (not_1_out, ADH[7]);
  RAM #(.addrWidth(15)) ram_1 (
    .addr({ADH[6:0], ADL}), .we(and_1_out), .oe(1'b1), .clk(Clk), .din(DI), .dout(ram_1_dout));
  and and_1 (and_1_out, WE, not_1_out);
  ROM #(.addrWidth(15)) rom_1 (.addr({ADH[6:0], ADL}), .data(rom_1_data));
  assign controlled_buffer_1_out = not_2_out ? ram_1_dout : 8'bz;  // Controlled_Buffer controlled_buffer_1
  not not_2 (not_2_out, ADH[7]);
  assign DO = OE ? controlled_buffer_1_out : 8'bz;  // Controlled_Buffer controlled_buffer_2
  assign controlled_buffer_1_out = ADH[7] ? rom_1_data : 8'bz;  // Controlled_Buffer controlled_buffer_3
endmodule

module XY (
  input  Clk,
  input  Reset,
  input  [7:0] DBI,
  input  XOE,
  input  XWE,
  input  YOE,
  input  YWE,
  output [7:0] DBO
);

  wire [7:0] register_1_q, register_2_q;

  Register register_1 (.D(DBI), .en(XWE), .clk(Clk), .Q(register_1_q), .clr(Reset));
  Register register_2 (.D(DBI), .en(YWE), .clk(Clk), .Q(register_2_q), .clr(Reset));
  assign DBO = XOE ? register_1_q : 8'bz;  // Controlled_Buffer controlled_buffer_1
  assign DBO = YOE ? register_2_q : 8'bz;  // Controlled_Buffer controlled_buffer_2
endmodule

module CSD (
  input  [7:0] Opcode,
  output PCE,
  output PCI,
  output PCO,
  output LAI,
  output LAO,
  output HAI,
  output HAO,
  output SPI,
  output SPO,
  output MEI,
  output MEO,
  output IRI,
  output ARI,
  output ARO,
  output XRI,
  output XRO,
  output YRI,
  output YRO,
  output SRI,
  output SRO,
  output RFI,
  output CFI,
  output IFS,
  output IFC,
  output HFS,
  output ZFO,
  output CFO,
  output EFO,
  output LFO,
  output GFO,
  output IFO,
  output AAD,
  output ASU,
  output AMU,
  output ADI,
  output AAN,
  output AIO,
  output AXO,
  output ASL,
  output ASR,
  output ANO,
  output AIN,
  output ADE,
  output ALO
);

  wire [47:44] rom_1_data;

  ROM #(.dataWidth(48)) rom_1 (
    .addr(Opcode),
    .data({rom_1_data, ALO, ADE, AIN, ANO, ASR, ASL, AXO, AIO, AAN, ADI, AMU, ASU, AAD, IFO, GFO, LFO, EFO, CFO, ZFO, HFS, IFC, IFS, CFI, RFI, SRO, SRI, YRO, YRI, XRO, XRI, ARO, ARI, IRI, MEO, MEI, SPO, SPI, HAO, HAI, LAO, LAI, PCO, PCI, PCE}));
endmodule

module ALU (
  input  [3:0] OpS,
  input  [7:0] DBI,
  input  [7:0] AI,
  output [7:0] RO,
  output [7:0] AO,
  output C,
  output Z
);

  wire adder_1_cout, adder_2_cout, and_1_out, and_2_out, demultiplexer_1_out1, demultiplexer_1_out2,
       demultiplexer_1_out3, demultiplexer_1_out4, demultiplexer_1_out5, demultiplexer_1_out6,
       demultiplexer_1_out7, demultiplexer_1_out8, demultiplexer_1_out9, demultiplexer_1_out10,
       demultiplexer_1_out11, demultiplexer_1_out12, subtractor_1_bout, subtractor_2_bout;
  wire [7:0] adder_1_out, adder_2_out, and_3_out, divider_1_out, divider_1_rem, multiplier_1_cout,
       multiplier_1_out, not_1_out, or_1_out, shifter_1_out, shifter_2_out, subtractor_1_out,
       subtractor_2_out, xor_1_out;

  assign AO = demultiplexer_1_out1 ? adder_1_out : 8'bz;  // Controlled_Buffer controlled_buffer_1
  Adder adder_1 (.a(AI), .b(DBI), .out(adder_1_out), .cout(adder_1_cout));  // open: cin
  assign C = demultiplexer_1_out1 ? adder_1_cout : 1'bz;  // Controlled_Buffer controlled_buffer_2
  assign AO = demultiplexer_1_out2 ? subtractor_1_out : 8'bz;  // Controlled_Buffer controlled_buffer_3
  Subtractor subtractor_1 (.a(AI), .b(DBI), .out(subtractor_1_out), .bout(subtractor_1_bout));  // open: bin
  assign C = demultiplexer_1_out2 ? subtractor_1_bout : 1'bz;  // Controlled_Buffer controlled_buffer_4
  assign AO = demultiplexer_1_out3 ? multiplier_1_out : 8'bz;  // Controlled_Buffer controlled_buffer_5
  Multiplier multiplier_1 (.a(AI), .b(DBI), .out(multiplier_1_out), .cout(multiplier_1_cout));  // open: cin
  assign AO = demultiplexer_1_out4 ? divider_1_out : 8'bz;  // Controlled_Buffer controlled_buffer_6
  Divider divider_1 (.a(AI), .b(DBI), .out(divider_1_out), .rem(divider_1_rem));  // open: upper
  Demultiplexer #(.select(4)) demultiplexer_1 (
    .out1(demultiplexer_1_out1), .out2(demultiplexer_1_out2), .out3(demultiplexer_1_out3),
    .out4(demultiplexer_1_out4), .out5(demultiplexer_1_out5), .out6(demultiplexer_1_out6),
    .out7(demultiplexer_1_out7), .out8(demultiplexer_1_out8), .out9(demultiplexer_1_out9),
    .out10(demultiplexer_1_out10), .out11(demultiplexer_1_out11), .out12(demultiplexer_1_out12), .in(1'b1),
    .sel(OpS));  // open: out0, out13, out14, out15
  and and_1 (and_1_out, multiplier_1_cout[0], multiplier_1_cout[1], multiplier_1_cout[2], multiplier_1_cout[3], multiplier_1_cout[4], multiplier_1_cout[5], multiplier_1_cout[6], multiplier_1_cout[7]);
  assign C = demultiplexer_1_out3 ? and_1_out : 1'bz;  // Controlled_Buffer controlled_buffer_7
  and and_2 (and_2_out, divider_1_rem[0], divider_1_rem[1], divider_1_rem[2], divider_1_rem[3], divider_1_rem[4], divider_1_rem[5], divider_1_rem[6], divider_1_rem[7]);
  assign C = demultiplexer_1_out4 ? and_2_out : 1'bz;  // Controlled_Buffer controlled_buffer_8
  assign and_3_out = AI & DBI;  // AND_Gate and_3, 8 bits wide
  assign AO = demultiplexer_1_out5 ? and_3_out : 8'bz;  // Controlled_Buffer controlled_buffer_9
  assign or_1_out = AI | DBI;  // OR_Gate or_1, 8 bits wide
  assign AO = demultiplexer_1_out6 ? or_1_out : 8'bz;  // Controlled_Buffer controlled_buffer_10
  assign xor_1_out = AI ^ DBI;  // XOR_Gate xor_1, 8 bits wide
  assign AO = demultiplexer_1_out7 ? xor_1_out : 8'bz;  // Controlled_Buffer controlled_buffer_11
  assign AO = demultiplexer_1_out8 ? shifter_1_out : 8'bz;  // Controlled_Buffer controlled_buffer_12
  Shifter shifter_1 (.in(AI), .\dist (DBI[2:0]), .out(shifter_1_out));
  assign AO = demultiplexer_1_out9 ? shifter_2_out : 8'bz;  // Controlled_Buffer controlled_buffer_13
  Shifter #(.shift("lr")) shifter_2 (.in(AI), .\dist (DBI[2:0]), .out(shifter_2_out));
  assign not_1_out = ~AI;  // NOT_Gate not_1, 8 bits wide
  assign AO = demultiplexer_1_out10 ? not_1_out : 8'bz;  // Controlled_Buffer controlled_buffer_14
  assign AO = demultiplexer_1_out11 ? adder_2_out : 8'bz;  // Controlled_Buffer controlled_buffer_15
  Adder adder_2 (.a(AI), .b({8{1'b0}}), .out(adder_2_out), .cin(1'b1), .cout(adder_2_cout));
  assign C = demultiplexer_1_out11 ? adder_2_cout : 1'bz;  // Controlled_Buffer controlled_buffer_16
  assign AO = demultiplexer_1_out12 ? subtractor_2_out : 8'bz;  // Controlled_Buffer controlled_buffer_17
  Subtractor subtractor_2 (.a(AI), .b({8{1'b0}}), .out(subtractor_2_out), .bin(1'b1), .bout(subtractor_2_bout));
  assign C = demultiplexer_1_out12 ? subtractor_2_bout : 1'bz;  // Controlled_Buffer controlled_buffer_18
  nor nor_1 (Z, AO[0], AO[1], AO[2], AO[3], AO[4], AO[5], AO[6], AO[7]);

  assign RO = AO;
endmodule

module IR (
  input  [7:0] DI,
  input  WE,
  input  Clk,
  input  Reset,
  output [7:0] DO
);

  Register register_1 (.D(DI), .en(WE), .clk(Clk), .Q(DO), .clr(Reset));
endmodule

module AR (
  input  Clk,
  input  Rst,
  input  OE,
  input  [7:0] ADLI,
  input  LWE,
  input  HWE,
  output [7:0] ADLO,
  output [7:0] ADHO
);

  wire [7:0] register_1_q, register_2_q;

  Register register_1 (.D(ADLI), .en(LWE), .clk(Clk), .Q(register_1_q), .clr(Rst));
  Register register_2 (.D(ADLI), .en(HWE), .clk(Clk), .Q(register_2_q), .clr(Rst));
  assign ADLO = OE ? register_1_q : 8'bz;  // Controlled_Buffer controlled_buffer_1
  assign ADHO = OE ? register_2_q : 8'bz;  // Controlled_Buffer controlled_buffer_2
endmodule

module DP (
  input  Clk,
  input  Rst,
  input  [7:0] ADLI,
  input  [7:0] ADHI,
  input  WE,
  output [7:0] ADLO,
  output [7:0] ADHO
);

  Register #(.width(16)) register_1 (.D({ADHI, ADLI}), .en(WE), .clk(Clk), .Q({ADHO, ADLO}), .clr(Rst));
endmodule

module SP (
  input  IE,
  input  DE,
  input  AOE,
  input  [7:0] DI,
  input  DOE,
  input  WE,
  input  Clk,
  input  Rst,
  output [7:0] AHO,
  output [7:0] ALO,
  output [7:0] DO
);

  wire not_1_out, xor_1_out;
  wire [7:0] counter_1_q;

  not not_1 (not_1_out, DE);
  xor xor_1 (xor_1_out, IE, DE);
  Counter counter_1 (
    .load(WE), .D(DI), .count(xor_1_out), .Q(counter_1_q), .up(not_1_out), .clk(Clk), .clr(Rst));  // open: carry
  assign AHO = AOE ? 8'h1 : 8'bz;  // Controlled_Buffer controlled_buffer_1
  assign ALO = AOE ? counter_1_q : 8'bz;  // Controlled_Buffer controlled_buffer_2
  assign DO = DOE ? counter_1_q : 8'bz;  // Controlled_Buffer controlled_buffer_3
endmodule

module JSD (
  input  WEI,
  input  JE,
  input  IJE,
  output WEO
);

  wire multiplexer_1_out, not_1_out;

  Multiplexer multiplexer_1 (.in0(JE), .in1(not_1_out), .out(multiplexer_1_out), .sel(IJE));
  Pull_Resistor #(.pull(1)) pull_resistor_1 (.node(multiplexer_1_out));
  not not_1 (not_1_out, JE);
  and and_1 (WEO, WEI, multiplexer_1_out);
endmodule

module SR (
  input  [4:0] FS,
  input  [7:0] DI,
  input  WE,
  input  Clk,
  input  Rst,
  output [7:0] DO,
  output FO,
  output IO,
  output HO
);

  Register register_1 (.D(DI), .en(WE), .clk(Clk), .Q(DO), .clr(Rst));
  assign FO = FS[0] ? DO[0] : 1'bz;  // Controlled_Buffer controlled_buffer_1
  assign FO = FS[1] ? DO[1] : 1'bz;  // Controlled_Buffer controlled_buffer_2
  assign FO = FS[2] ? DO[2] : 1'bz;  // Controlled_Buffer controlled_buffer_3
  assign FO = FS[3] ? DO[3] : 1'bz;  // Controlled_Buffer controlled_buffer_4
  assign FO = FS[4] ? DO[4] : 1'bz;  // Controlled_Buffer controlled_buffer_5

  assign HO = DO[7];
  assign IO = DO[6];
endmodule

module Latch (
  input  CL,
  input  CH,
  input  [7:0] ADLI,
  input  [7:0] DBI,
  input  [7:0] ADHI,
  output [7:0] ADLO,
  output [7:0] DBO,
  output [7:0] ADHO
);

  assign ADLO = CL ? DBI : 8'bz;  // Controlled_Buffer controlled_buffer_1
  assign DBO = CL ? ADLI : 8'bz;  // Controlled_Buffer controlled_buffer_2
  assign DBO = CH ? ADHI : 8'bz;  // Controlled_Buffer controlled_buffer_3
  assign ADHO = CH ? DBI : 8'bz;  // Controlled_Buffer controlled_buffer_4
endmodule

module R (
  input  RWE,
  input  DWE,
  input  OE,
  input  [7:0] DBI,
  input  [7:0] RI,
  input  Clk,
  input  Rst,
  output [7:0] out_8
);

  wire or_1_out;
  wire [7:0] controlled_buffer_1_out, register_1_q;

  assign controlled_buffer_1_out = RWE ? RI : 8'bz;  // Controlled_Buffer controlled_buffer_1
  or or_1 (or_1_out, DWE, RWE);
  Register register_1 (.D(controlled_buffer_1_out), .en(or_1_out), .clk(Clk), .Q(register_1_q), .clr(Rst));
  assign controlled_buffer_1_out = DWE ? DBI : 8'bz;  // Controlled_Buffer controlled_buffer_2
  assign out_8 = OE ? register_1_q : 8'bz;  // Controlled_Buffer controlled_buffer_3
endmodule

module A (
  input  RWE,
  input  DWE,
  input  ROE,
  input  DOE,
  input  [7:0] DBI,
  input  [7:0] RI,
  input  Clk,
  input  Rst,
  output [7:0] DBO,
  output [7:0] RO
);

  wire or_1_out;
  wire [7:0] controlled_buffer_1_out, register_1_q;

  assign controlled_buffer_1_out = RWE ? RI : 8'bz;  // Controlled_Buffer controlled_buffer_1
  or or_1 (or_1_out, DWE, RWE);
  Register register_1 (.D(controlled_buffer_1_out), .en(or_1_out), .clk(Clk), .Q(register_1_q), .clr(Rst));
  assign controlled_buffer_1_out = DWE ? DBI : 8'bz;  // Controlled_Buffer controlled_buffer_2
  assign DBO = DOE ? register_1_q : 8'bz;  // Controlled_Buffer controlled_buffer_3
  assign RO = ROE ? register_1_q : 8'bz;  // Controlled_Buffer controlled_buffer_4
endmodule
